// Logisim project mata3820171.circ as structural Verilog
module main (
  input  [7:0] in_1,
  input  [7:0] in_2,
  input  [1:0] in_3,
  input  [1:0] in_4,
  output [7:0] out_5,
  output [7:0] R1,
  output [7:0] R2,
  output [7:0] out_8,
  output [7:0] out_9,
  output [7:0] out_10,
  output [7:0] out_11,
  output [7:0] out_12,
  output [7:0] out_13,
  output [7:0] out_14,
  output [7:0] out_15,
  output [7:0] out_16,
  output [7:0] out_17,
  output [7:0] out_18,
  output [7:0] out_19,
  output [7:0] out_20,
  output [7:0] out_21,
  output [7:0] out_22,
  output [7:0] out_23,
  output [7:0] out_24,
  output [7:0] out_25,
  output [7:0] out_26,
  output [7:0] out_27,
  output [7:0] out_28,
  output [7:0] out_29,
  output [7:0] out_30,
  output out_31,
  output [7:0] out_32,
  output [7:0] out_33,
  output [7:0] out_34,
  output [7:0] out_35,
  output [7:0] out_36,
  output [7:0] out_37,
  output [7:0] out_38,
  output [7:0] out_39,
  output out_40,
  output [7:0] out_41,
  output [7:0] out_42,
  output [7:0] out_43,
  output out_44,
  output [7:0] out_45,
  output [7:0] out_46,
  output [7:0] out_47,
  output out_48,
  output [7:0] out_49,
  output [7:0] out_50,
  output out_51
);

  wire adder_1_cout, clock_1_out, comparator_4_eq, comparator_4_lt, comparator_5_eq, comparator_5_gt,
       undriven;
  wire [7:0] multiplexer_1_out, multiplexer_2_out, undriven_2, undriven_3;

  Clock clock_1 (.out(clock_1_out));
  Register register_1 (.D(in_2), .en(undriven), .Q(out_5), .clk(clock_1_out));  // open: clr
  Multiplexer #(.select(2), .width(8)) multiplexer_1 (
    .in0(out_5), .in1(R1), .in2(undriven_2), .in3(undriven_3), .out(multiplexer_1_out), .sel(in_3));  // open: en
  Register register_2 (.D(in_1), .Q(R1), .clk(clock_1_out));  // open: en, clr
  Register register_3 (.D(undriven_2), .Q(R2), .clk(clock_1_out));  // open: en, clr
  Multiplexer #(.select(2), .width(8)) multiplexer_2 (
    .in0(out_5), .in1(R1), .in2(undriven_2), .in3(undriven_3), .out(multiplexer_2_out), .sel(in_4));  // open: en
  Register register_4 (.D(undriven_3), .Q(out_8), .clk(clock_1_out));  // open: en, clr
  Demultiplexer #(.select(4), .width(8)) demultiplexer_1 (
    .out0(out_10), .out1(out_11), .out2(out_13), .out3(out_14), .out4(out_15), .out5(out_17), .out6(out_18),
    .out7(out_20), .out8(out_21), .out9(out_22), .out10(out_24), .out11(out_25), .out12(out_26),
    .out13(out_26), .out14(out_26), .out15(out_26), .in(multiplexer_2_out), .sel(4'b1010));  // open: en
  Demultiplexer #(.select(4), .width(8)) demultiplexer_2 (
    .out0(out_32), .out1(out_33), .out2(out_34), .out3(out_35), .out4(out_36), .out5(out_37), .out6(out_38),
    .out7(out_39), .out8(out_41), .out9(out_42), .out10(out_43), .out11(out_45), .out12(out_46),
    .out13(out_47), .out14(out_49), .out15(out_50), .in(multiplexer_1_out), .sel(4'b1010));  // open: en
  assign out_9 = out_10 & out_32;  // AND_Gate and_1, 8 bits wide
  assign out_12 = out_11 | out_33;  // OR_Gate or_1, 8 bits wide
  assign out_16 = out_13 ^ out_34;  // XOR_Gate xor_1, 8 bits wide
  assign out_19 = ~out_35;  // NOT_Gate not_1, 8 bits wide
  Adder adder_1 (.a(out_15), .b(out_36), .out(out_23), .cout(adder_1_cout));  // open: cin
  Subtractor subtractor_1 (.a(out_17), .b(out_37), .out(out_27));  // open: bin, bout
  Comparator comparator_1 (.a(out_38), .b(out_18), .eq(out_31));  // open: gt, lt
  Comparator comparator_2 (.a(out_39), .b(out_20), .lt(out_40));  // open: gt, eq
  Comparator comparator_3 (.a(out_41), .b(out_21), .eq(out_44));  // open: gt, lt
  Comparator comparator_4 (.a(out_42), .b(out_22), .eq(comparator_4_eq), .lt(comparator_4_lt));  // open: gt
  Comparator comparator_5 (.a(out_43), .b(out_24), .gt(comparator_5_gt), .eq(comparator_5_eq));  // open: lt
  or or_2 (out_48, comparator_4_eq, comparator_4_lt);
  or or_3 (out_51, comparator_5_gt, comparator_5_eq);

  assign out_28 = out_26;
  assign out_29 = out_26;
  assign out_30 = out_26;

  // Notes on the sheet:
  //   R0
  //   R3
  //   R2
  //   R1
endmodule
