// Logisim project memoria.circ as structural Verilog: 1 circuit, main circuit main
module main (
  input  in_1,
  input  in_2,
  input  in_3,
  output [15:0] out_4,
  output [7:0] out_5,
  output [7:0] out_6
);

  wire clock_1_out;

  Clock clock_1 (.out(clock_1_out));
  Counter #(.width(16), .max('hffff)) counter_1 (
    .Q(out_4), .clk(clock_1_out), .clr(in_1));  // open: load, D, count, carry
  BitSelector #(.width(16), .group(8)) bitselector_1 (.in(out_4), .out(out_6), .sel(in_3));
  RAM #(.addrWidth(16), .bus("separate")) ram_1 (
    .addr(out_4), .din(out_6), .data(out_5), .clk(clock_1_out), .ld(in_2));  // open: str, sel, clr

  // Notes on the sheet:
  //   endereçamento
  //   entrada de dados
endmodule
